# Fritzing sketch jessica_fritz (saved by Fritzing 0.9.3b)

parts:
  Composant1 = Arduino Nano (Rev3.0) (ICSP)
  DFPlayer_Mini1 = DFPlayer MINI [package="DIP (Dual Inline) [THT]"]
  SP1 = SPEAKER [package=pcb_mount_speaker]
  LED1 = RGB LED (com. cathode, rgb) [package="5 mm [THT]"]
  1K = Resistor [tolerance=±5% resistance=220 package="2512 [SMD]"]
  VCC1 = Battery block 9V

nets (from the schematic view):
  GND: Composant1.GND, DFPlayer_Mini1.GND, VCC1.-
  N1: Composant1.D3, LED1.blue_anode
  N2: Composant1.D4, LED1.green_anode
  N3: Composant1.D5, LED1.red_anode
  N4: Composant1.D6, DFPlayer_Mini1.BUSY
  N5: Composant1.D9, DFPlayer_Mini1.TX
  N6: Composant1.VIN, VCC1.+
  5V: Composant1.5V, DFPlayer_Mini1.VCC
  N7: DFPlayer_Mini1.RX, 1K.Pin_1
  N8: DFPlayer_Mini1.SPK1, SP1.+
  N9: DFPlayer_Mini1.SPK2, SP1.-

custom parts:
  DFPlayer MINI: MP3 module by DFRobot.com for playing Music from an SD-Card. Supports WAV and MP3 files.
